# Fritzing sketch 라즈베리파이 회로도 (saved by Fritzing 0.9.3b)
breadboards: 1

parts:
  Raspberry_Pi_2 = Raspberry Pi 3 [part_number=RPI-3-V1.2]
  LCD1 = LCD screen
  R1 = Rotary Potentiometer (Large) [package=THT]
  R2 = Resistor [tolerance=±5% resistance=220 package="0805 [SMD]"]
  LED2 = 7-SEGMENT-4DIGIT-YOUNGSUN [package=7-segment-4digit-youngsun-longpads]

nets:
  N1: Raspberry_Pi_2.GPIO2, LED2.DIG2
  N2: Raspberry_Pi_2.GPIO3, LED2.D
  N3: Raspberry_Pi_2.GIPO4, LED2.E
  N4: Raspberry_Pi_2.GIPO17, LED2.DIG3
  N5: Raspberry_Pi_2.GIPO27, LED2.DP
  N6: Raspberry_Pi_2.GIPO22, LED2.APOS-A
  N7: Raspberry_Pi_2.GIPO10, LED2.F
  N8: Raspberry_Pi_2.GIPO9, LED2.COL-C
  N9: Raspberry_Pi_2.GIPO11, LED2.C
  N10: Raspberry_Pi_2.GIPO5, LED2.A
  N11: Raspberry_Pi_2.GIPO6, LED2.G
  N12: Raspberry_Pi_2.GIPO26, LED2.COL-A
  N13: Raspberry_Pi_2.GIPO7, LCD1.RS
  N14: Raspberry_Pi_2.GIPO8, LCD1.E
  N15: Raspberry_Pi_2.GIPO25, LCD1.DB4
  N16: Raspberry_Pi_2.GIPO24, LCD1.DB5
  N17: Raspberry_Pi_2.GIPO23, LCD1.DB6
  N18: Raspberry_Pi_2.GIPO18, LCD1.DB7
  GND: Raspberry_Pi_2.GND, LCD1.VSS, LCD1.R/W, LCD1.LED-, R1.leg2
  5V: Raspberry_Pi_2.5V, LCD1.VDD, R1.leg1, R2.Pin_1
  N19: LCD1.V0, R1.wiper
  N20: LCD1.LED+, R2.Pin_0

notes:
  4 digit 7 segment display 핀 12개
